// Logisim project cpu.circ as structural Verilog: 10 circuits, main circuit main
module main (
  input  MANUAL,
  input  CLK_ENB
);

  wire A_IN, A_OUT, alu_1_cout, ALU_OUT, B_IN, bcd_to_7_segment_decoder_3_p1, binary_to_bcd_converter_1_p2,
       binary_to_bcd_converter_1_p4, clk_1_clk_out, clock_1_out, COUNTER_ENABLE, COUNTER_OUT, decoder_1_out0,
       decoder_1_out1, decoder_1_out2, decoder_1_out3, decoder_1_out4, decoder_1_out5, decoder_1_out6,
       decoder_2_out0, decoder_2_out1, decoder_2_out2, decoder_2_out3, decoder_2_out4, decoder_2_out5,
       decoder_2_out6, decoder_2_out7, decoder_2_out8, decoder_2_out9, decoder_2_out10, decoder_2_out11,
       decoder_2_out12, decoder_2_out13, decoder_2_out14, decoder_2_out15, FLAGS_IN, HLT, INR_IN, INR_OUT,
       JUMP, MAR_IN, not_1_out, or_1_out, OUT_IN, RAM_IN, RAM_OUT, RESET_out, SUB, undriven, zero_1_zero_out;
  wire [3:0] INSTRUCTION_REG_r1_always_out, MAR_r1_always_out, prgcntr_1_pc_always_out, STEPCTR_pc_always_out;
  wire [7:0] A_r1_always_out, alu_1_always_out, B_r1_always_out, binary_to_bcd_converter_1_p1,
       INSTRUCTION_REG_r1_address_out, RAM_always_out;
  wire [8:3] flags_1_zero_out;

  not not_1 (not_1_out, clk_1_clk_out);
  or or_1 (or_1_out, decoder_1_out6, RESET_out);
  PRGCNTR STEPCTR (
    .RESET(or_1_out), .JUMP(1'b0), .COUNTER_ENABLE(1'b1), .CLK_IN(not_1_out), .COUNTER_OUT(1'b1),
    .PC_ALWAYS_OUT(STEPCTR_pc_always_out));  // open: PC_ADDRESS_IN, PC_ADDRESS_OUT
  Decoder #(.select(4)) decoder_1 (
    .out0(decoder_1_out0), .out1(decoder_1_out1), .out2(decoder_1_out2), .out3(decoder_1_out3),
    .out4(decoder_1_out4), .out5(decoder_1_out5), .out6(decoder_1_out6), .sel(STEPCTR_pc_always_out));  // open: out7, out8, out9, out10, out11, out12, out13, out14, out15, en
  LED led_1 ();  // open: in
  LED led_2 ();  // open: in
  LED led_3 ();  // open: in
  LED led_4 ();  // open: in
  LED led_5 ();  // open: in
  LED led_6 ();  // open: in
  REGISTRI INSTRUCTION_REG (
    .R1_ADDRESS_IN(INSTRUCTION_REG_r1_address_out), .R1_IN_ENABLE(INR_IN), .CLK(clk_1_clk_out),
    .R1_OUT_ENABLE(INR_OUT), .R1_RESET(RESET_out),
    .R1_ALWAYS_OUT({flags_1_zero_out[6:3], INSTRUCTION_REG_r1_always_out}),
    .R1_ADDRESS_OUT(INSTRUCTION_REG_r1_address_out));
  // Probe on RAM_always_out
  // Probe on MAR_r1_always_out
  Button RESET (.out(RESET_out));
  REGISTRS MAR (
    .R1_ADDRESS_IN(INSTRUCTION_REG_r1_address_out[3:0]), .R1_IN_ENABLE(MAR_IN), .CLK(clk_1_clk_out),
    .R1_RESET(RESET_out), .R1_ALWAYS_OUT(MAR_r1_always_out));  // open: R1_OUT_ENABLE, R1_ADDRESS_OUT
  RAMC RAM (
    .CLK(clk_1_clk_out), .DATA(INSTRUCTION_REG_r1_address_out), .ADDRESS_IN(MAR_r1_always_out),
    .STORE(RAM_IN), .RAM_OUT_ENABLE(RAM_OUT), .ALWAYS_OUT(RAM_always_out),
    .DATA_OUT(INSTRUCTION_REG_r1_address_out));
  ROM #(.addrWidth(9), .dataWidth(16)) rom_1 (
    .addr({flags_1_zero_out, STEPCTR_pc_always_out[2:0]}),
    .data({FLAGS_IN, JUMP, COUNTER_OUT, COUNTER_ENABLE, OUT_IN, B_IN, SUB, ALU_OUT, A_OUT, A_IN, INR_IN, INR_OUT, RAM_OUT, RAM_IN, MAR_IN, HLT}));
  Pull_Resistor pull_resistor_1 (.node(INSTRUCTION_REG_r1_address_out[7]));
  LED led_7 (.in(flags_1_zero_out[8]));
  Clock clock_1 (.out(clock_1_out));
  Pull_Resistor pull_resistor_2 (.node(INSTRUCTION_REG_r1_address_out[6]));
  Pull_Resistor pull_resistor_3 (.node(INSTRUCTION_REG_r1_address_out[5]));
  Pull_Resistor pull_resistor_4 (.node(INSTRUCTION_REG_r1_address_out[4]));
  Pull_Resistor pull_resistor_5 (.node(INSTRUCTION_REG_r1_address_out[3]));
  LED led_8 (.in(flags_1_zero_out[7]));
  LED led_9 (.in(flags_1_zero_out[6]));
  LED led_10 (.in(flags_1_zero_out[5]));
  LED led_11 (.in(flags_1_zero_out[4]));
  Pull_Resistor pull_resistor_6 (.node(INSTRUCTION_REG_r1_address_out[2]));
  Pull_Resistor pull_resistor_7 (.node(INSTRUCTION_REG_r1_address_out[1]));
  Pull_Resistor pull_resistor_8 (.node(INSTRUCTION_REG_r1_address_out[0]));
  LED led_12 (.in(flags_1_zero_out[3]));
  LED led_13 (.in(STEPCTR_pc_always_out[2]));
  LED led_14 (.in(STEPCTR_pc_always_out[1]));
  LED led_15 (.in(STEPCTR_pc_always_out[0]));
  LED led_16 (.in(HLT));
  LED led_17 (.in(MAR_IN));
  LED led_18 (.in(RAM_IN));
  LED led_19 (.in(RAM_OUT));
  LED led_20 (.in(INR_OUT));
  LED led_21 (.in(INR_IN));
  LED led_22 (.in(A_IN));
  LED led_23 (.in(A_OUT));
  LED led_24 (.in(ALU_OUT));
  LED led_25 (.in(SUB));
  LED led_26 (.in(B_IN));
  LED led_27 (.in(OUT_IN));
  LED led_28 (.in(COUNTER_ENABLE));
  LED led_29 (.in(COUNTER_OUT));
  LED led_30 (.in(JUMP));
  LED led_31 (.in(FLAGS_IN));
  LED led_32 (.in(INSTRUCTION_REG_r1_address_out[7]));
  LED led_33 (.in(INSTRUCTION_REG_r1_address_out[6]));
  LED led_34 (.in(INSTRUCTION_REG_r1_address_out[5]));
  LED led_35 (.in(INSTRUCTION_REG_r1_address_out[4]));
  LED led_36 (.in(INSTRUCTION_REG_r1_address_out[3]));
  LED led_37 (.in(INSTRUCTION_REG_r1_address_out[2]));
  LED led_38 (.in(INSTRUCTION_REG_r1_address_out[1]));
  LED led_39 (.in(INSTRUCTION_REG_r1_address_out[0]));
  CLK clk_1 (.CLK_IN(clock_1_out), .CLK_ENB(CLK_ENB), .MANUAL(MANUAL), .HALT(HLT), .CLK_OUT(clk_1_clk_out));
  // BCD_to_7_Segment_decoder bcd_to_7_segment_decoder_1: pin names not known
  _7_Segment_Display u_7_segment_display_1 ();  // open: g, f, a, b, e, d, c, dp
  // Binary_to_BCD_converter #(.binvalue(8)) binary_to_bcd_converter_1: pin names not known; wires that end beside it: binary_to_bcd_converter_1_p1, binary_to_bcd_converter_1_p2, binary_to_bcd_converter_1_p2, binary_to_bcd_converter_1_p4
  // BCD_to_7_Segment_decoder bcd_to_7_segment_decoder_2: pin names not known; wires that end beside it: binary_to_bcd_converter_1_p4
  _7_Segment_Display u_7_segment_display_2 ();  // open: g, f, a, b, e, d, c, dp
  // BCD_to_7_Segment_decoder bcd_to_7_segment_decoder_3: pin names not known; wires that end beside it: bcd_to_7_segment_decoder_3_p1, bcd_to_7_segment_decoder_3_p1
  _7_Segment_Display u_7_segment_display_3 ();  // open: g, f, a, b, e, d, c, dp
  Pull_Resistor pull_resistor_9 (.node(FLAGS_IN));
  Pull_Resistor pull_resistor_10 (.node(JUMP));
  Pull_Resistor pull_resistor_11 (.node(COUNTER_OUT));
  Pull_Resistor pull_resistor_12 (.node(COUNTER_ENABLE));
  Pull_Resistor pull_resistor_13 (.node(OUT_IN));
  // Probe on A_r1_always_out
  Pull_Resistor pull_resistor_14 (.node(B_IN));
  Pull_Resistor pull_resistor_15 (.node(SUB));
  Pull_Resistor pull_resistor_16 (.node(ALU_OUT));
  Pull_Resistor pull_resistor_17 (.node(A_OUT));
  Pull_Resistor pull_resistor_18 (.node(A_IN));
  Pull_Resistor pull_resistor_19 (.node(INR_IN));
  Pull_Resistor pull_resistor_20 (.node(INR_OUT));
  Pull_Resistor pull_resistor_21 (.node(RAM_OUT));
  PRGCNTR prgcntr_1 (
    .RESET(RESET_out), .JUMP(JUMP), .COUNTER_ENABLE(COUNTER_ENABLE), .CLK_IN(clk_1_clk_out),
    .PC_ADDRESS_IN(INSTRUCTION_REG_r1_address_out[3:0]), .COUNTER_OUT(COUNTER_OUT),
    .PC_ALWAYS_OUT(prgcntr_1_pc_always_out), .PC_ADDRESS_OUT(INSTRUCTION_REG_r1_address_out[3:0]));
  REGSTR A (
    .R1_ADDRESS_IN(INSTRUCTION_REG_r1_address_out), .R1_IN_ENABLE(A_IN), .CLK(clk_1_clk_out),
    .R1_OUT_ENABLE(A_OUT), .R1_RESET(RESET_out), .R1_ALWAYS_OUT(A_r1_always_out),
    .R1_ADDRESS_OUT(INSTRUCTION_REG_r1_address_out));
  ALU alu_1 (
    .CIN(undriven), .A_INP(A_r1_always_out), .B_INP(B_r1_always_out), .SUB(SUB), .OUTPUT_ENABLE(ALU_OUT),
    .ALWAYS_OUT(alu_1_always_out), .ALU_OUT(INSTRUCTION_REG_r1_address_out), .COUT(alu_1_cout));
  REGSTR B (
    .R1_ADDRESS_IN(INSTRUCTION_REG_r1_address_out), .R1_IN_ENABLE(B_IN), .CLK(clk_1_clk_out),
    .R1_RESET(RESET_out), .R1_ALWAYS_OUT(B_r1_always_out), .R1_ADDRESS_OUT(INSTRUCTION_REG_r1_address_out));  // open: R1_OUT_ENABLE
  REGSTR OUTPUTR (
    .R1_ADDRESS_IN(INSTRUCTION_REG_r1_address_out), .R1_IN_ENABLE(OUT_IN), .CLK(clk_1_clk_out),
    .R1_OUT_ENABLE(1'b1), .R1_RESET(RESET_out), .R1_ADDRESS_OUT(binary_to_bcd_converter_1_p1));  // open: R1_ALWAYS_OUT
  Pull_Resistor pull_resistor_22 (.node(RAM_IN));
  Pull_Resistor pull_resistor_23 (.node(MAR_IN));
  Pull_Resistor pull_resistor_24 (.node(HLT));
  // Probe on alu_1_always_out
  LED led_40 (.in(decoder_2_out15));
  LED led_41 (.in(decoder_2_out14));
  LED led_42 (.in(decoder_2_out13));
  LED led_43 (.in(decoder_2_out12));
  LED led_44 (.in(decoder_2_out11));
  LED led_45 (.in(decoder_2_out10));
  LED led_46 (.in(decoder_2_out9));
  ZERO zero_1 (.ZERO_IN(alu_1_always_out), .ZERO_OUT(zero_1_zero_out));
  // Probe on B_r1_always_out
  LED led_47 (.in(decoder_2_out8));
  LED led_48 (.in(decoder_2_out7));
  LED led_49 (.in(decoder_2_out6));
  LED led_50 (.in(decoder_2_out5));
  LED led_51 (.in(decoder_2_out4));
  LED led_52 (.in(decoder_2_out3));
  LED led_53 (.in(decoder_2_out2));
  LED led_54 (.in(decoder_2_out1));
  LED led_55 (.in(decoder_2_out0));
  FLAGS flags_1 (
    .CARRY_IN(alu_1_cout), .ZERO_IN(zero_1_zero_out), .CLK(clk_1_clk_out), .STORE(FLAGS_IN),
    .RESET(RESET_out), .CARRY_OUT(flags_1_zero_out[8]), .ZERO_OUT(flags_1_zero_out[7]));
  Decoder #(.select(4)) decoder_2 (
    .out0(decoder_2_out0), .out1(decoder_2_out1), .out2(decoder_2_out2), .out3(decoder_2_out3),
    .out4(decoder_2_out4), .out5(decoder_2_out5), .out6(decoder_2_out6), .out7(decoder_2_out7),
    .out8(decoder_2_out8), .out9(decoder_2_out9), .out10(decoder_2_out10), .out11(decoder_2_out11),
    .out12(decoder_2_out12), .out13(decoder_2_out13), .out14(decoder_2_out14), .out15(decoder_2_out15),
    .sel(prgcntr_1_pc_always_out));  // open: en

  // Notes on the sheet:
  //   STEP COUNTER
  //   contents of rom_1 (hex, n*v repeats v):
  //   2002 28 1000 5*0 2002 28 1000 12 48 0 0 0 2002 28 1000 12 408 140 0 0 2002 28 1000 880 4*0 2002 28
  //   1000 12 84 0 0 0 2002 28 4010 2002
  //   INSTRUCTION REG
  //   BUS
  //   CONTROL UNIT
  //   PROGRAM COUNTER
endmodule

module REGSTR (
  input  [7:0] R1_ADDRESS_IN,
  input  R1_IN_ENABLE,
  input  CLK,
  input  R1_OUT_ENABLE,
  input  R1_RESET,
  output [7:0] R1_ALWAYS_OUT,
  output [7:0] R1_ADDRESS_OUT
);

  Register register_1 (.D(R1_ADDRESS_IN), .en(R1_IN_ENABLE), .clk(CLK), .Q(R1_ALWAYS_OUT), .clr(R1_RESET));
  assign R1_ADDRESS_OUT = R1_OUT_ENABLE ? R1_ALWAYS_OUT : 8'bz;  // Controlled_Buffer controlled_buffer_1
endmodule

module CLK (
  input  CLK_IN,
  input  CLK_ENB,
  input  MANUAL,
  input  HALT,
  output CLK_OUT
);

  wire and_1_out, and_2_out, not_1_out, not_2_out, or_1_out;

  not not_1 (not_1_out, CLK_ENB);
  not not_2 (not_2_out, HALT);
  and and_1 (and_1_out, CLK_IN, CLK_ENB);
  and and_2 (and_2_out, not_1_out, MANUAL);
  or or_1 (or_1_out, and_1_out, and_2_out);
  and and_3 (CLK_OUT, or_1_out, not_2_out);
endmodule

module PRGCNTR (
  input  RESET,
  input  JUMP,
  input  COUNTER_ENABLE,
  input  CLK_IN,
  input  [3:0] PC_ADDRESS_IN,
  input  COUNTER_OUT,
  output [3:0] PC_ALWAYS_OUT,
  output [3:0] PC_ADDRESS_OUT
);

  Counter #(.max('hf), .width(4)) counter_1 (
    .clr(RESET), .load(JUMP), .up(COUNTER_ENABLE), .count(COUNTER_ENABLE), .clk(CLK_IN), .D(PC_ADDRESS_IN),
    .Q(PC_ALWAYS_OUT));  // open: carry
  assign PC_ADDRESS_OUT = COUNTER_OUT ? PC_ALWAYS_OUT : 4'bz;  // Controlled_Buffer controlled_buffer_1
endmodule

module RAMC (
  input  CLK,
  input  [7:0] DATA,
  input  [3:0] ADDRESS_IN,
  input  STORE,
  input  RAM_OUT_ENABLE,
  output [7:0] ALWAYS_OUT,
  output [7:0] DATA_OUT
);

  wire and_1_out, and_2_out, and_3_out, and_4_out, and_5_out, and_6_out, and_7_out, and_8_out, and_9_out,
       and_10_out, and_11_out, and_12_out, and_13_out, and_14_out, and_15_out, and_16_out, decoder_1_out0,
       decoder_1_out1, decoder_1_out2, decoder_1_out3, decoder_1_out4, decoder_1_out5, decoder_1_out6,
       decoder_1_out7, decoder_1_out8, decoder_1_out9, decoder_1_out10, decoder_1_out11, decoder_1_out12,
       decoder_1_out13, decoder_1_out14, decoder_1_out15;
  wire [7:0] demultiplexer_1_out0, demultiplexer_1_out1, demultiplexer_1_out2, demultiplexer_1_out3,
       demultiplexer_1_out4, demultiplexer_1_out5, demultiplexer_1_out6, demultiplexer_1_out7,
       demultiplexer_1_out8, demultiplexer_1_out9, demultiplexer_1_out10, demultiplexer_1_out11,
       demultiplexer_1_out12, demultiplexer_1_out13, demultiplexer_1_out14, demultiplexer_1_out15,
       register_1_q, register_2_q, register_3_q, register_4_q, register_5_q, register_6_q, register_7_q,
       register_8_q, register_9_q, register_10_q, register_11_q, register_12_q, register_13_q, register_14_q,
       register_15_q, register_16_q;

  Demultiplexer #(.select(4), .width(8)) demultiplexer_1 (
    .out0(demultiplexer_1_out0), .out1(demultiplexer_1_out1), .out2(demultiplexer_1_out2),
    .out3(demultiplexer_1_out3), .out4(demultiplexer_1_out4), .out5(demultiplexer_1_out5),
    .out6(demultiplexer_1_out6), .out7(demultiplexer_1_out7), .out8(demultiplexer_1_out8),
    .out9(demultiplexer_1_out9), .out10(demultiplexer_1_out10), .out11(demultiplexer_1_out11),
    .out12(demultiplexer_1_out12), .out13(demultiplexer_1_out13), .out14(demultiplexer_1_out14),
    .out15(demultiplexer_1_out15), .in(DATA), .sel(ADDRESS_IN));
  Decoder #(.select(4)) decoder_1 (
    .out0(decoder_1_out0), .out1(decoder_1_out1), .out2(decoder_1_out2), .out3(decoder_1_out3),
    .out4(decoder_1_out4), .out5(decoder_1_out5), .out6(decoder_1_out6), .out7(decoder_1_out7),
    .out8(decoder_1_out8), .out9(decoder_1_out9), .out10(decoder_1_out10), .out11(decoder_1_out11),
    .out12(decoder_1_out12), .out13(decoder_1_out13), .out14(decoder_1_out14), .out15(decoder_1_out15),
    .sel(ADDRESS_IN));  // open: en
  and and_1 (and_1_out, decoder_1_out0, STORE);
  and and_2 (and_2_out, decoder_1_out1, STORE);
  and and_3 (and_3_out, decoder_1_out2, STORE);
  and and_4 (and_4_out, decoder_1_out3, STORE);
  and and_5 (and_5_out, decoder_1_out4, STORE);
  and and_6 (and_6_out, decoder_1_out5, STORE);
  and and_7 (and_7_out, decoder_1_out6, STORE);
  and and_8 (and_8_out, decoder_1_out7, STORE);
  and and_9 (and_9_out, decoder_1_out8, STORE);
  and and_10 (and_10_out, decoder_1_out9, STORE);
  and and_11 (and_11_out, decoder_1_out10, STORE);
  and and_12 (and_12_out, decoder_1_out11, STORE);
  and and_13 (and_13_out, decoder_1_out12, STORE);
  and and_14 (and_14_out, decoder_1_out13, STORE);
  and and_15 (and_15_out, decoder_1_out14, STORE);
  and and_16 (and_16_out, decoder_1_out15, STORE);
  Register register_1 (.D(demultiplexer_1_out0), .en(and_1_out), .clk(CLK), .Q(register_1_q));  // open: clr
  Register register_2 (.D(demultiplexer_1_out1), .en(and_2_out), .clk(CLK), .Q(register_2_q));  // open: clr
  Register register_3 (.D(demultiplexer_1_out2), .en(and_3_out), .clk(CLK), .Q(register_3_q));  // open: clr
  Register register_4 (.D(demultiplexer_1_out3), .en(and_4_out), .clk(CLK), .Q(register_4_q));  // open: clr
  Register register_5 (.D(demultiplexer_1_out4), .en(and_5_out), .clk(CLK), .Q(register_5_q));  // open: clr
  Register register_6 (.D(demultiplexer_1_out5), .en(and_6_out), .clk(CLK), .Q(register_6_q));  // open: clr
  Register register_7 (.D(demultiplexer_1_out6), .en(and_7_out), .clk(CLK), .Q(register_7_q));  // open: clr
  Register register_8 (.D(demultiplexer_1_out7), .en(and_8_out), .clk(CLK), .Q(register_8_q));  // open: clr
  Register register_9 (.D(demultiplexer_1_out8), .en(and_9_out), .clk(CLK), .Q(register_9_q));  // open: clr
  Register register_10 (.D(demultiplexer_1_out9), .en(and_10_out), .clk(CLK), .Q(register_10_q));  // open: clr
  Register register_11 (.D(demultiplexer_1_out10), .en(and_11_out), .clk(CLK), .Q(register_11_q));  // open: clr
  Register register_12 (.D(demultiplexer_1_out11), .en(and_12_out), .clk(CLK), .Q(register_12_q));  // open: clr
  Register register_13 (.D(demultiplexer_1_out12), .en(and_13_out), .clk(CLK), .Q(register_13_q));  // open: clr
  Register register_14 (.D(demultiplexer_1_out13), .en(and_14_out), .clk(CLK), .Q(register_14_q));  // open: clr
  Register register_15 (.D(demultiplexer_1_out14), .en(and_15_out), .clk(CLK), .Q(register_15_q));  // open: clr
  Register register_16 (.D(demultiplexer_1_out15), .en(and_16_out), .clk(CLK), .Q(register_16_q));  // open: clr
  Multiplexer #(.select(4), .width(8)) multiplexer_1 (
    .in0(register_1_q), .in1(register_2_q), .in2(register_3_q), .in3(register_4_q), .in4(register_5_q),
    .in5(register_6_q), .in6(register_7_q), .in7(register_8_q), .in8(register_9_q), .in9(register_10_q),
    .in10(register_11_q), .in11(register_12_q), .in12(register_13_q), .in13(register_14_q),
    .in14(register_15_q), .in15(register_16_q), .out(ALWAYS_OUT), .sel(ADDRESS_IN));
  assign DATA_OUT = RAM_OUT_ENABLE ? ALWAYS_OUT : 8'bz;  // Controlled_Buffer controlled_buffer_1
endmodule

module ALU (
  input  CIN,
  input  [7:0] A_INP,
  input  [7:0] B_INP,
  input  SUB,
  input  OUTPUT_ENABLE,
  output [7:0] ALWAYS_OUT,
  output [7:0] ALU_OUT,
  output COUT
);

  wire not_1_out;
  wire [7:0] controlled_buffer_1_out, xor_1_out;

  assign controlled_buffer_1_out = SUB ? {8{1'b1}} : 8'bz;  // Controlled_Buffer controlled_buffer_1
  assign controlled_buffer_1_out = not_1_out ? {8{1'b0}} : 8'bz;  // Controlled_Buffer controlled_buffer_2
  not not_1 (not_1_out, SUB);
  assign xor_1_out = B_INP ^ controlled_buffer_1_out;  // XOR_Gate xor_1, 8 bits wide
  Adder adder_1 (.a(A_INP), .b(xor_1_out), .out(ALWAYS_OUT), .cin(CIN), .cout(COUT));
  assign ALU_OUT = OUTPUT_ENABLE ? ALWAYS_OUT : 8'bz;  // Controlled_Buffer controlled_buffer_3
endmodule

module REGISTRS (
  input  [3:0] R1_ADDRESS_IN,
  input  R1_IN_ENABLE,
  input  CLK,
  input  R1_OUT_ENABLE,
  input  R1_RESET,
  output [3:0] R1_ALWAYS_OUT,
  output [3:0] R1_ADDRESS_OUT
);

  Register #(.width(4)) register_1 (.D(R1_ADDRESS_IN), .en(R1_IN_ENABLE), .clk(CLK), .Q(R1_ALWAYS_OUT), .clr(R1_RESET));
  assign R1_ADDRESS_OUT = R1_OUT_ENABLE ? R1_ALWAYS_OUT : 4'bz;  // Controlled_Buffer controlled_buffer_1
endmodule

module REGISTRI (
  input  [7:0] R1_ADDRESS_IN,
  input  R1_IN_ENABLE,
  input  CLK,
  input  R1_OUT_ENABLE,
  input  R1_RESET,
  output [7:0] R1_ALWAYS_OUT,
  output [7:0] R1_ADDRESS_OUT
);

  wire [7:4] pull_resistor_1_node;

  Register register_1 (.D(R1_ADDRESS_IN), .en(R1_IN_ENABLE), .clk(CLK), .Q(R1_ALWAYS_OUT), .clr(R1_RESET));
  Pull_Resistor pull_resistor_1 (.node(pull_resistor_1_node[4]));
  Pull_Resistor pull_resistor_2 (.node(pull_resistor_1_node[5]));
  Pull_Resistor pull_resistor_3 (.node(pull_resistor_1_node[6]));
  Pull_Resistor pull_resistor_4 (.node(pull_resistor_1_node[7]));
  assign R1_ADDRESS_OUT = R1_OUT_ENABLE ? {pull_resistor_1_node, R1_ALWAYS_OUT[3:0]} : 8'bz;  // Controlled_Buffer controlled_buffer_1
endmodule

module ZERO (
  input  [7:0] ZERO_IN,
  output ZERO_OUT
);

  or or_1 (ZERO_OUT, ZERO_IN[0], ZERO_IN[1], ZERO_IN[2], ZERO_IN[3], ZERO_IN[4], ZERO_IN[5], ZERO_IN[6], ZERO_IN[7]);
endmodule

module FLAGS (
  input  CARRY_IN,
  input  ZERO_IN,
  input  CLK,
  input  STORE,
  input  RESET,
  output CARRY_OUT,
  output ZERO_OUT
);

  Register #(.width(1)) register_1 (.D(CARRY_IN), .en(STORE), .clk(CLK), .Q(CARRY_OUT), .clr(RESET));
  Register #(.width(1)) register_2 (.D(ZERO_IN), .en(STORE), .clk(CLK), .Q(ZERO_OUT), .clr(RESET));
endmodule
